# Fritzing sketch esp32 and bmp180 (saved by Fritzing 0.9.3b)

parts:
  MCU1 = Wemos Lolin32lite
  Part1 = Barometric Pressure Sensor - BMP180 Breakout (GY-68)

nets:
  N1: MCU1.pin_1, Part1.VCC
  N2: MCU1.pin_15, MCU1.pin_34, Part1.GND
  N3: MCU1.pin_29, Part1.SDA
  N4: MCU1.pin_32, Part1.SCL

custom parts:
  Wemos Lolin32lite: Wemos Lolin32 pro wifi and blue tooth board based on the ESP-32 cpu, digital I/Os 22, analog inputs 6, analog outputs 2, clock 240mhz, Flash 4Mbytes, PSRAM 4MB, microSD card slot, lipo battery charger (500ma connection broken out on breadboard but not pcb), usb.
