# Fritzing sketch esp32 and bmp280 (saved by Fritzing 0.9.3b)

parts:
  MCU1 = Wemos Lolin32lite
  Part3 = Adafruit_BMP280

nets:
  N1: MCU1.pin_1, Part3.3.3V
  N2: MCU1.pin_29, Part3.SDI/SDA
  N3: MCU1.pin_32, Part3.SCK/SCL
  N4: MCU1.pin_34, Part3.GND

custom parts:
  Wemos Lolin32lite: Wemos Lolin32 pro wifi and blue tooth board based on the ESP-32 cpu, digital I/Os 22, analog inputs 6, analog outputs 2, clock 240mhz, Flash 4Mbytes, PSRAM 4MB, microSD card slot, lipo battery charger (500ma connection broken out on breadboard but not pcb), usb.
  Adafruit_BMP280: Bosch has stepped up their game with their new BMP280 sensor, an environmental sensor with temperature, barometric pressure that is the next generation upgrade to the BMP085/BMP180/BMP183. This sensor is great for all sorts of weather sensing and can even be used in both I2C and SPI! This precision sensor from Bosch is the best low-cost, precision sensing solution for measuring barometric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
