# Fritzing sketch esp32 and hdc1008 (saved by Fritzing 0.9.3b)

parts:
  MCU1 = Wemos Lolin32lite
  Part2 = Adafruit HDC1008 Temperature Humidity Sensor [part_number="Adafruit #2635"]

nets:
  N1: MCU1.pin_1, Part2.VDD
  N2: MCU1.pin_15, MCU1.pin_21, MCU1.pin_34, Part2.GND
  N3: MCU1.pin_29, Part2.SDA
  N4: MCU1.pin_32, Part2.SCL

custom parts:
  Wemos Lolin32lite: Wemos Lolin32 pro wifi and blue tooth board based on the ESP-32 cpu, digital I/Os 22, analog inputs 6, analog outputs 2, clock 240mhz, Flash 4Mbytes, PSRAM 4MB, microSD card slot, lipo battery charger (500ma connection broken out on breadboard but not pcb), usb.
  Adafruit HDC1008 Temperature Humidity Sensor: This I2C digital humidity sensor is a fairly accurate and intelligent alternative to the much simpler Humidity and Temperature Sensor - SHT15 Breakout It has a typical accuracy of ±4% with an operating range that's optimized from 10% to 80% RH. Operation outside this range is still possible - just the accuracy might drop a bit. The temperature output has a typical accuracy of ±0.2°C from -20~85°C.
