# Fritzing sketch esp32 and si1145 (saved by Fritzing 0.9.3b)

parts:
  MCU1 = Wemos Lolin32lite
  Part1 = SI1145 Digital UV Index + IR + Visible Light Sensor [part_number=1777]

nets:
  N1: MCU1.pin_1, Part1.+3V3
  N2: MCU1.pin_21, MCU1.pin_34, Part1.GND
  N3: MCU1.pin_29, Part1.SDA
  N4: MCU1.pin_32, Part1.SCL

custom parts:
  Wemos Lolin32lite: Wemos Lolin32 pro wifi and blue tooth board based on the ESP-32 cpu, digital I/Os 22, analog inputs 6, analog outputs 2, clock 240mhz, Flash 4Mbytes, PSRAM 4MB, microSD card slot, lipo battery charger (500ma connection broken out on breadboard but not pcb), usb.
  SI1145 Digital UV Index + IR + Visible Light Sensor: The SI1145 is a new sensor from SiLabs with a calibrated light sensing algorithm that can calculate UV Index. It doesn't contain an actual UV sensing element, instead it approximates it based on visible & IR light from the sun. We took this outside a couple days and compared the calculated UV index with the news-reported index and found it was very accurate! It's a digital sensor that works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
