# Fritzing sketch feather and ADS1015 (saved by Fritzing 0.9.3b)

parts:
  Part13 = Adafruit Feather M0 Express [part_number="Adafruit #3403"]
  Part17 = Adafruit ADS1015 12Bit I2C ADC [part_number="Adafruit #1083"]

nets:
  GND: Part13.GND, Part17.GND
  +3V3: Part13.+3V3, Part17.VDD
  N1: Part13.SCL, Part17.SCL
  N2: Part13.SDA, Part17.SDA

custom parts:
  Adafruit Feather M0 Express: We love all our Feathers equally, but this Feather is very special. It's our first Feather that is specifically designed for use with CircuitPython! CircuitPython is our beginner-oriented flavor of MicroPython - and as the name hints at, its a small but full-featured version of the popular Python programming language specifically for use with circuitry and electronics. That doesn't mean you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
  Adafruit ADS1015 12Bit I2C ADC: For microcontrollers without an analog-to-digital converter or when you want a higher-precision ADC, the ADS1015 provides 12-bit precision at 3300 samples/second over I2C. The chip can be configured as 4 single-ended input channels, or two differential channels. As a nice bonus, it even includes a programmable gain amplifier, up to x16, to help boost up smaller single/differential signals to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
