# Fritzing sketch feather and AM2302 (saved by Fritzing 0.9.3b)

parts:
  Part13 = Adafruit Feather M0 Express [part_number="Adafruit #3403"]
  Part14 = DHT22 module

nets:
  GND: Part13.GND, Part14.GND
  +3V3: Part13.+3V3, Part14.VCC
  N1: Part13.D6, Part14.DATA

custom parts:
  Adafruit Feather M0 Express: We love all our Feathers equally, but this Feather is very special. It's our first Feather that is specifically designed for use with CircuitPython! CircuitPython is our beginner-oriented flavor of MicroPython - and as the name hints at, its a small but full-featured version of the popular Python programming language specifically for use with circuitry and electronics. That doesn't mean you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
