# Fritzing sketch feather and CCS811 (saved by Fritzing 0.9.3b)

parts:
  Part13 = Adafruit Feather M0 Express [part_number="Adafruit #3403"]
  Part15 = Adafruit CCS811

nets:
  GND: Part13.GND, Part15.GND, Part15.!WAKE
  +3V3: Part13.+3V3, Part15.3.3V
  N1: Part13.SCL, Part15.SCL
  N2: Part13.SDA, Part15.SDA

custom parts:
  Adafruit Feather M0 Express: We love all our Feathers equally, but this Feather is very special. It's our first Feather that is specifically designed for use with CircuitPython! CircuitPython is our beginner-oriented flavor of MicroPython - and as the name hints at, its a small but full-featured version of the popular Python programming language specifically for use with circuitry and electronics. That doesn't mean you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
