# Fritzing sketch feather and DHT11 (saved by Fritzing 0.9.3b)

parts:
  Part13 = Adafruit Feather M0 Express [part_number="Adafruit #3403"]
  DHT11_1 = DHT11 module

nets:
  GND: Part13.GND, DHT11_1.GND
  +3V3: Part13.+3V3, DHT11_1.VCC
  N1: Part13.D6, DHT11_1.DATA

custom parts:
  Adafruit Feather M0 Express: We love all our Feathers equally, but this Feather is very special. It's our first Feather that is specifically designed for use with CircuitPython! CircuitPython is our beginner-oriented flavor of MicroPython - and as the name hints at, its a small but full-featured version of the popular Python programming language specifically for use with circuitry and electronics. That doesn't mean you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
  DHT11 module: DHT11 black pcb module
