# Fritzing sketch feather and LPS25 (saved by Fritzing 0.9.3b)

parts:
  Part13 = Adafruit Feather M0 Express [part_number="Adafruit #3403"]
  Adafruit_LPS2X1 = Adafruit-LPS2X

nets:
  GND: Part13.GND, Adafruit_LPS2X1.GND
  +3V3: Part13.+3V3, Adafruit_LPS2X1.3.3V
  N1: Part13.SCL, Adafruit_LPS2X1.SCK/SCL
  N2: Part13.SDA, Adafruit_LPS2X1.SDI/SDA

custom parts:
  Adafruit Feather M0 Express: We love all our Feathers equally, but this Feather is very special. It's our first Feather that is specifically designed for use with CircuitPython! CircuitPython is our beginner-oriented flavor of MicroPython - and as the name hints at, its a small but full-featured version of the popular Python programming language specifically for use with circuitry and electronics. That doesn't mean you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
  Adafruit-LPS2X: I've got news for you: we're all sitting at the bottom of an ocean of nitrogen, oxygen, and other gasses. Just like a whale would have trouble breathing if it weren't under an ocean of ocean water, we would have a hard time getting oxygen and nitrogen into our lungs if we weren't swimming in it. Because we're used to being under all this air, for us it's relatively normal to us and we don't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
