# Fritzing sketch feather and MLX90393 (saved by Fritzing 0.9.3b)

parts:
  Part13 = Adafruit Feather M0 Express [part_number="Adafruit #3403"]
  Part20 = Adafruit MLX90393 Magnetometer [part_number="Adafruit #4022"]

nets:
  GND: Part13.GND, Part20.GND
  +3V3: Part13.+3V3, Part20.3.3V
  N1: Part13.SCL, Part20.SCL
  N2: Part13.SDA, Part20.SDA

custom parts:
  Adafruit Feather M0 Express: We love all our Feathers equally, but this Feather is very special. It's our first Feather that is specifically designed for use with CircuitPython! CircuitPython is our beginner-oriented flavor of MicroPython - and as the name hints at, its a small but full-featured version of the popular Python programming language specifically for use with circuitry and electronics. That doesn't mean you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
