# Fritzing sketch feather and MPL3115A2 (saved by Fritzing 0.9.3b)

parts:
  Part13 = Adafruit Feather M0 Express [part_number="Adafruit #3403"]
  Part15 = MPL3115A2 I2C Barometric Pressure, Altitude, Temperature Sensor

nets:
  GND: Part13.GND, Part15.GND
  +3V3: Part13.+3V3, Part15.+3V3
  N1: Part13.SCL, Part15.SCL
  N2: Part13.SDA, Part15.SDA

custom parts:
  Adafruit Feather M0 Express: We love all our Feathers equally, but this Feather is very special. It's our first Feather that is specifically designed for use with CircuitPython! CircuitPython is our beginner-oriented flavor of MicroPython - and as the name hints at, its a small but full-featured version of the popular Python programming language specifically for use with circuitry and electronics. That doesn't mean you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
  MPL3115A2 I2C Barometric Pressure, Altitude, Temperature Sensor: This pressure sensor from Freescale is a great low-cost sensing solution for precision measurement of barometric pressure and altitude. The MPL3115A2 has a typical 1.5 Pascal resolution, which can resolve altitude at 0.3 meters (compare to the BMP180 which can do 0.17m). It has some upsides compared to the BMP180, such as interrupt outputs for ultra-low power usage, and its also a heck of a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
