# Fritzing sketch feather and veml6070 (saved by Fritzing 0.9.3b)

parts:
  Part13 = Adafruit Feather M0 Express [part_number="Adafruit #3403"]
  Part16 = Adafruit VEML6075 UV Sensor Breakout [part_number=3964]

nets:
  GND: Part13.GND, Part16.GND
  +3V3: Part13.+3V3, Part16.3.3V
  N1: Part13.SCL, Part16.SCL
  N2: Part13.SDA, Part16.SDA

custom parts:
  Adafruit Feather M0 Express: We love all our Feathers equally, but this Feather is very special. It's our first Feather that is specifically designed for use with CircuitPython! CircuitPython is our beginner-oriented flavor of MicroPython - and as the name hints at, its a small but full-featured version of the popular Python programming language specifically for use with circuitry and electronics. That doesn't mean you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
  Adafruit VEML6075 UV Sensor Breakout: This little sensor is a great way to add UVA and UVB light sensing to any microcontroller project. The VEML6075 from Vishay has both true UVA and UVB band light sensors and an I2C-controlled ADC that will take readings and integrate them. The sensor also comes with calibration registers so you can easily convert the UVA/UVB readings into the UV Index. Compared to our other UV sensors, this one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
