# Fritzing sketch micropython and bmp180 (saved by Fritzing 0.9.3b)

parts:
  pyboard1 = Micro Python pyboard [part_number=PYBv10b]
  Part1 = Adafruit BMP180

nets:
  N1: pyboard1.X9, Part1.SCL
  N2: pyboard1.X10, Part1.SDA
  N3: pyboard1.Y14_GND, Part1.GND
  N4: pyboard1.Y15_3V3, Part1.+3V3

custom parts:
  Adafruit BMP180: This precision sensor from Bosch is the best low-cost sensing solution for measuring barometric pressure and temperature. Because pressure changes with altitude you can also use it as an altimeter! The sensor is soldered onto a PCB with a 3.3V regulator, I2C level shifter and pull-up resistors on the I2C pins. The BMP180 is the next-generation of sensors from Bosch, and replaces the BMP085.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
