# Fritzing sketch pyboard and hc-sr04 (saved by Fritzing 0.9.3b)

parts:
  pyboard1 = Micro Python pyboard [part_number=PYBv10b]
  HC-SR04_Sensor_1 = HC-SR04 Ultrasonic Distance Sensor

nets:
  N1: pyboard1.X1, HC-SR04_Sensor_1.TRIG
  N2: pyboard1.X2, HC-SR04_Sensor_1.ECHO
  N3: pyboard1.Y14_GND, HC-SR04_Sensor_1.GND
  N4: pyboard1.Y15_3V3, HC-SR04_Sensor_1.VCC
